// Logisim project 8bit_cpu.circ as structural Verilog: 4 circuits, main circuit ULA
module ULA (
  input  [7:0] A,
  input  [7:0] B,
  input  [2:0] Select_Op,
  output [7:0] Output
);

  wire [7:0] adder_1_out, adder_2_out, adder_3_out, and_1_out, or_1_out, subtractor_1_out;

  Adder adder_1 (.a(A), .b(8'h1), .out(adder_1_out));  // open: cin, cout
  Adder adder_2 (.a(B), .b(8'h1), .out(adder_2_out));  // open: cin, cout
  Adder adder_3 (.a(A), .b(B), .out(adder_3_out));  // open: cin, cout
  Subtractor subtractor_1 (.a(A), .b(B), .out(subtractor_1_out));  // open: bin, bout
  assign and_1_out = A & A;  // AND_Gate and_1, 8 bits wide
  assign or_1_out = A | B;  // OR_Gate or_1, 8 bits wide
  Multiplexer #(.select(3), .width(8)) multiplexer_1 (
    .in0(A), .in1(B), .in2(adder_1_out), .in3(adder_2_out), .in4(adder_3_out), .in5(subtractor_1_out),
    .in6(and_1_out), .in7(or_1_out), .out(Output), .sel(Select_Op));  // open: en
endmodule

module Datapath (
  input  Program_Counter_Register_Enable,
  input  [7:0] External_Memory_Data_Bus,
  input  Memory_Byte_Register_Enable,
  input  Register_Output_Enable,
  input  Register_B_Enable,
  input  [7:0] External_Input,
  input  Register_A_Enablel,
  input  [1:0] MUX_Fonte_B,
  input  Clock,
  input  Reset,
  input  [2:0] AluOp,
  output [7:0] External_Memory_Address_Bus,
  output [7:0] Output_Register
);

  wire [7:0] Memory_Byte_Register_q, multiplexer_1_out, Register_A_q, Register_B_q, ula_1_output;

  Register Program_Counter (
    .D(ula_1_output), .en(Program_Counter_Register_Enable), .Q(External_Memory_Address_Bus), .clk(Clock),
    .clr(Reset));
  Register Memory_Byte_Register (
    .D(External_Memory_Data_Bus), .en(Memory_Byte_Register_Enable), .Q(Memory_Byte_Register_q), .clk(Clock),
    .clr(Reset));
  Register Output (.D(ula_1_output), .en(Register_Output_Enable), .Q(Output_Register), .clk(Clock), .clr(Reset));
  Register Register_B (.D(ula_1_output), .en(Register_B_Enable), .Q(Register_B_q), .clk(Clock), .clr(Reset));
  Register Register_A (.D(ula_1_output), .en(Register_A_Enablel), .Q(Register_A_q), .clk(Clock), .clr(Reset));
  Multiplexer #(.select(2), .width(8)) multiplexer_1 (
    .in0(Register_B_q), .in1(Memory_Byte_Register_q), .in2(External_Memory_Address_Bus),
    .in3(External_Input), .out(multiplexer_1_out), .sel(MUX_Fonte_B), .en(1'b1));
  ULA ula_1 (.Output(ula_1_output), .A(Register_A_q), .B(multiplexer_1_out), .Select_Op(AluOp));
endmodule

module Unidade_de_Controle (
  input  in_1,
  input  [7:0] External_Input,
  input  [7:0] External_Memory_Data,
  input  Clock,
  output [7:0] External_Memory_Address,
  output [7:0] ULA_Output
);

  wire [1:0] MIR_q;
  wire [2:0] MIR_q_3;
  wire [4:0] bit_extender_1_out, MIR_q_4, MPC_q, multiplexer_1_out;
  wire [10:2] MIR_q_2;
  wire [15:0] rom_1_data;

  Datapath datapath_1 (
    .Program_Counter_Register_Enable(MIR_q_2[6]), .External_Memory_Data_Bus(External_Memory_Data),
    .Memory_Byte_Register_Enable(MIR_q_2[5]), .Register_Output_Enable(MIR_q_2[4]),
    .Register_B_Enable(MIR_q_2[3]), .Register_A_Enablel(MIR_q_2[2]),
    .External_Memory_Address_Bus(External_Memory_Address), .MUX_Fonte_B(MIR_q), .AluOp(MIR_q_3),
    .External_Input(External_Input), .Clock(Clock), .Reset(in_1), .Output_Register(ULA_Output));
  Bit_Extender #(.out_width(5)) bit_extender_1 (.in(ULA_Output), .out(bit_extender_1_out));
  Register #(.width(5)) MPC (.D(multiplexer_1_out), .Q(MPC_q), .clk(Clock));  // open: en, clr
  Multiplexer #(.width(5)) multiplexer_1 (
    .in0(MIR_q_4), .in1(bit_extender_1_out), .out(multiplexer_1_out), .sel(MIR_q_2[10]));  // open: en
  ROM #(.addrWidth(5), .dataWidth(16)) rom_1 (.addr(MPC_q), .data(rom_1_data));  // open: sel
  Register #(.width(16)) MIR (
    .D(rom_1_data), .Q({MIR_q_4, MIR_q_2[10], MIR_q_3, MIR_q_2[6:2], MIR_q}), .clk(Clock));  // open: en, clr

  // Notes on the sheet:
  //   contents of rom_1 (hex, n*v repeats v):
  //   a10
endmodule

module CPU (
  input  [7:0] Input_Externo,
  input  in_2,
  output [7:0] Output
);

  wire clock_1_out;
  wire [7:0] rom_1_data, unidade_de_controle_1_external_memory_address;

  ROM rom_1 (.addr(unidade_de_controle_1_external_memory_address), .data(rom_1_data));  // open: sel
  Unidade_de_Controle unidade_de_controle_1 (
    .Clock(clock_1_out), .in_1(in_2), .External_Input(Input_Externo),
    .External_Memory_Address(unidade_de_controle_1_external_memory_address),
    .External_Memory_Data(rom_1_data), .ULA_Output(Output));
  Clock clock_1 (.out(clock_1_out));
endmodule
